# Fritzing sketch LoLGamePad Fritzing (saved by Fritzing 0.9.2b)
breadboards: 1

parts:
  Pro_Micro1 = Pro Micro  # not connected
  S1 = Round Pushbutton
  S2 = Round Pushbutton  # not connected
  S3 = Round Pushbutton
  S4 = Round Pushbutton
  S5 = Round Pushbutton
  S6 = Round Pushbutton
  S7 = Round Pushbutton
  S8 = Round Pushbutton
  S9 = Round Pushbutton
  S10 = Round Pushbutton
  LED2 = RGB LED (com. cathode, rgb) [package="5 mm [THT]"]
  MIC1 = Microphone
  R1 = Resistor [tolerance=±5% resistance=220 package=THT]
  Composant1 = Thumb Joystick

nets:
  N1: S1.leg1, S3.leg1, S4.leg1, S5.leg1, S6.leg1, S7.leg1, S8.leg1, S9.leg1, S10.leg1, MIC1.pin1, R1.Pin_0, Composant1.GND
  N2: LED2.common_cathode, R1.Pin_1

notes:
  4
  R
  F
  Z
  3
  2
  D
  1
  E
  A

custom parts:
  Pro Micro: The SparkFun Pro Micro is a complete USB-based microcontoller development system, in a very small footprint, capable of implementing many types of projects. All programming can be done via the USB port.
